// Digital circuit tarea1_Marianela_Arcila.dig as structural Verilog
module tarea1_Marianela_Arcila (
  input  E0,
  input  S0,
  input  S1,
  input  S2,
  input  E1,
  input  E2,
  input  E3,
  input  E4,
  input  E5,
  input  E6,
  input  E7,
  input  E0_2,
  input  S0_2,
  input  S1_2,
  input  SET,
  input  RESET,
  input  J,
  input  K,
  input  in_21,
  input  Set_2,
  input  Enable,
  input  Clear,
  input  Clock,
  input  D1,
  input  D2,
  input  D3,
  input  D4,
  input  Set_3,
  input  Enable_2,
  input  Clear_2,
  input  Clock_2,
  input  D5,
  input  D6,
  input  D7,
  input  D8,
  input  Set_4,
  input  Enable_3,
  input  Clear_3,
  input  Clock_3,
  input  D9,
  input  D10,
  input  D11,
  input  D12,
  output Q,
  output Q_2,
  output out_22,
  output out_23,
  output out_24,
  output out_25,
  output out_34,
  output out_35,
  output out_36,
  output out_37,
  output out_46,
  output out_47,
  output out_48,
  output out_49
);

  wire and_1_out, and_2_out, and_3_out, and_4_out, and_5_out, and_6_out, and_7_out, and_8_out, and_9_out,
       and_10_out, and_11_out, and_12_out, and_13_out, and_14_out, multiplexer_1_out, multiplexer_2_out,
       multiplexer_3_out, multiplexer_4_out, multiplexer_5_out, multiplexer_6_out, multiplexer_7_out,
       multiplexer_8_out, multiplexer_9_out, multiplexer_10_out, multiplexer_11_out, multiplexer_12_out,
       nand_1_out, nand_2_out, nor_1_out, nor_2_out, not_1_out, not_2_out, not_3_out, not_4_out, not_5_out,
       or_1_out, or_2_out, or_3_out, undriven;

  not not_1 (not_1_out, S0);
  not not_2 (not_2_out, S1);
  not not_3 (not_3_out, S2);
  and and_1 (and_1_out, E0, not_1_out, not_2_out, not_3_out);
  and and_2 (and_2_out, E1, S0, not_3_out, not_2_out);
  and and_3 (and_3_out, E2, not_1_out, S1, not_3_out);
  and and_4 (and_4_out, E3, S0, S1, not_3_out);
  and and_5 (and_5_out, E4, not_1_out, not_2_out, S2);
  and and_6 (and_6_out, E5, S0, not_2_out, S2);
  and and_7 (and_7_out, E6, S0, S1, not_3_out);
  and and_8 (and_8_out, E7, S0, S1, S2);
  or or_1 (or_1_out, and_1_out, and_2_out, and_3_out, and_4_out);
  or or_2 (or_2_out, and_5_out, and_6_out, and_7_out, and_8_out);
  and and_9 (and_9_out, or_1_out, or_1_out);
  and and_10 (and_10_out, or_2_out, or_2_out);
  or or_3 (or_3_out, and_9_out, and_10_out);
  LED Salida (.in(or_3_out));
  not not_4 (not_4_out, S0_2);
  not not_5 (not_5_out, S1_2);
  and and_11 (and_11_out, E0_2, not_4_out, not_5_out);
  and and_12 (and_12_out, E0_2, not_4_out, S1_2);
  and and_13 (and_13_out, E0_2, S0_2, not_5_out);
  and and_14 (and_14_out, E0_2, S0_2, S1_2);
  LED Y0 (.in(and_11_out));
  LED Y1 (.in(and_12_out));
  LED Y2 (.in(and_13_out));
  LED Y3 (.in(and_14_out));
  nand nand_1 (nand_1_out, Q_2, J, in_21);
  nand nand_2 (nand_2_out, in_21, K, Q);
  nor nor_1 (nor_1_out, SET, nor_2_out);
  nor nor_2 (nor_2_out, nor_1_out, RESET);
  nand nand_3 (Q, nand_1_out, Q_2);
  nand nand_4 (Q_2, Q, nand_2_out);
  LED u_Q (.in(nor_1_out));
  LED u_Q_2 (.in(nor_2_out));
  Multiplexer multiplexer_1 (.sel(Enable_3), .in_0(out_46), .in_1(D9), .out(multiplexer_1_out));
  Multiplexer multiplexer_2 (.sel(Enable), .in_0(out_22), .in_1(D1), .out(multiplexer_2_out));
  Multiplexer multiplexer_3 (.sel(Enable_2), .in_0(out_34), .in_1(D5), .out(multiplexer_3_out));
  D_FF_AS d_ff_as_1 (.Set(Set_4), .D(multiplexer_1_out), .C(Clock_3), .Clr(Clear_3), .Q(out_46));  // open: nQ
  D_FF_AS d_ff_as_2 (.Set(Set_2), .D(multiplexer_2_out), .C(Clock), .Clr(Clear), .Q(out_22));  // open: nQ
  D_FF_AS d_ff_as_3 (.Set(Set_3), .D(multiplexer_3_out), .C(Clock_2), .Clr(Clear_2), .Q(out_34));  // open: nQ
  Multiplexer multiplexer_4 (.sel(Enable_3), .in_0(out_47), .in_1(undriven), .out(multiplexer_4_out));
  Multiplexer multiplexer_5 (.sel(Enable), .in_0(out_23), .in_1(D2), .out(multiplexer_5_out));
  Multiplexer multiplexer_6 (.sel(Enable_2), .in_0(out_35), .in_1(D6), .out(multiplexer_6_out));
  D_FF_AS d_ff_as_4 (.Set(Set_4), .D(multiplexer_4_out), .C(Clock_3), .Clr(Clear_3), .Q(out_47));  // open: nQ
  D_FF_AS d_ff_as_5 (.Set(Set_2), .D(multiplexer_5_out), .C(Clock), .Clr(Clear), .Q(out_23));  // open: nQ
  D_FF_AS d_ff_as_6 (.Set(Set_3), .D(multiplexer_6_out), .C(Clock_2), .Clr(Clear_2), .Q(out_35));  // open: nQ
  Multiplexer multiplexer_7 (.sel(Enable_3), .in_0(out_48), .in_1(D11), .out(multiplexer_7_out));
  Multiplexer multiplexer_8 (.sel(Enable), .in_0(out_24), .in_1(D3), .out(multiplexer_8_out));
  Multiplexer multiplexer_9 (.sel(Enable_2), .in_0(out_36), .in_1(D7), .out(multiplexer_9_out));
  D_FF_AS d_ff_as_7 (.Set(Set_4), .D(multiplexer_7_out), .C(Clock_3), .Clr(Clear_3), .Q(out_48));  // open: nQ
  D_FF_AS d_ff_as_8 (.Set(Set_2), .D(multiplexer_8_out), .C(Clock), .Clr(Clear), .Q(out_24));  // open: nQ
  D_FF_AS d_ff_as_9 (.Set(Set_3), .D(multiplexer_9_out), .C(Clock_2), .Clr(Clear_2), .Q(out_36));  // open: nQ
  Multiplexer multiplexer_10 (.sel(Enable_3), .in_0(out_49), .in_1(D12), .out(multiplexer_10_out));
  Multiplexer multiplexer_11 (.sel(Enable), .in_0(out_25), .in_1(D4), .out(multiplexer_11_out));
  Multiplexer multiplexer_12 (.sel(Enable_2), .in_0(out_37), .in_1(D8), .out(multiplexer_12_out));
  D_FF_AS d_ff_as_10 (.Set(Set_4), .D(multiplexer_10_out), .C(Clock_3), .Clr(Clear_3), .Q(out_49));  // open: nQ
  D_FF_AS d_ff_as_11 (.Set(Set_2), .D(multiplexer_11_out), .C(Clock), .Clr(Clear), .Q(out_25));  // open: nQ
  D_FF_AS d_ff_as_12 (.Set(Set_3), .D(multiplexer_12_out), .C(Clock_2), .Clr(Clear_2), .Q(out_37));  // open: nQ

  // Notes on the sheet:
  //   Clock: Hz: 100
  //   Clock_2: Hz: 100
  //   Clock_3: Hz: 100
  //   Para crear el multiplexor de 8 entradas y una salida, se utilizaron dos multiplexores de 
  //   4 entradas, los cuales estan conectados a dos compuertas logicas AND que a su vez
  //   van unidas por una compuerta OR hacia la salida (una especie de multiplexor de dos entradas 1 salida),
  //   esto para poder relacionar los dos multiplexores a una salida unica
  //   Multiplexor de 8 Entradas 1 Salida
  //   En Demultiplexor tiene una entrada, la cual es trasmitida a una de las 4 salidas
  //   segun el tipo de combinacion de activacion  se se ecoja en los S0 y S1, este sistema
  //   tiene compuertas AND y para negar los valores de S se utilizan compuertas NOT
  //   Demultiplexor de 1 Entrada 4 Salidas
  //   Flip Flop RS
  //   Un flip flop RS es un sistema el cual tiene la capacidad de almacenar o borrar 1 bit de informacion
  //   tiene dos entradas una SET y otra RESET en donde se refrescan los estados de salida.
  //   Las compuertas NOR al tener ambas entradas en 1 estas generan una salida 0 por lo tanto
  //   al hacer las conexiones cruzadas solo una de las compuertas permite la trasmicion del dato a la salida
  //   El Flip Flop Jk tiene dos salidas Q y Q', al J igualarse a 1 
  //   y K a 0 el estado de Q cambia a 1, y cuando se invierte ocurre lo mismo
  //   para Q', luego al estar los dos activados, en teoria el estado de 
  //   ambos cambiaria, pero en este caso el programa queda en un estado oscilante
  //   Flip Flop JK
endmodule
